// Digital circuit mips.dig as structural Verilog
module mips (
  input  CLK,
  input  RST,
  output [31:0] PC,
  output [31:0] ALUResult,
  output [31:0] MemData
);

  wire beq, bne, Branch, BranchNe, Jal, Jump, JumpRegister, MemRead, MemToReg, MemWrite, PCSrc, RegWrite,
       UseShamt, zero;
  wire [1:0] ALUSrc, RegDst;
  wire [2:0] ALUOp;
  wire [3:0] Op;
  wire [4:0] RegWAddr;
  wire [5:0] funct;
  wire [15:6] immediate;
  wire [31:0] ALUMem, branch__offset, In1, In2, MemWD, NextPC, NPC0, NPC1, PCBranch, RegData1, RegWD,
       sign__imm, sign__shamt;
  wire [31:4] PCPlus4;
  wire [31:16] instr;
  wire [31:28] PCJump;

  and and_1 (bne, ~zero, BranchNe);  // And
  and and_2 (beq, zero, Branch);
  or or_1 (PCSrc, bne, beq);
  Shift32 #(.applicationType("IVERILOG")) u_Shift32 (.a(sign__imm), .shamt(32'h2), .out(branch__offset));
  Addr32_1 #(.applicationType("IVERILOG")) u_Addr32_1 (.a({PCPlus4, PCJump}), .b(branch__offset), .out(PCBranch));
  Multiplexer #(.Bits(32)) multiplexer_1 (.sel(PCSrc), .in_0({PCPlus4, PCJump}), .in_1(PCBranch), .out(NPC0));
  Multiplexer #(.Bits(32)) multiplexer_2 (.sel(JumpRegister), .in_0(NPC1), .in_1(ALUMem), .out(NextPC));
  BitExtender #(.inputBits(16), .outputBits(32)) bitextender_1 (.in({immediate, funct}), .out(sign__imm));
  BitExtender #(.inputBits(5), .outputBits(32)) bitextender_2 (.in(immediate[10:6]), .out(sign__shamt));
  Multiplexer #(.Bits(32)) multiplexer_3 (
    .sel(Jump), .in_0(NPC0), .in_1({PCJump, 2'b00, instr[25:16], immediate, funct}), .out(NPC1));
  Addr32_0 #(.applicationType("IVERILOG")) u_Addr32_0 (.a(PC), .b(32'h1), .out({PCPlus4, PCJump}));
  RegFile #(.applicationType("IVERILOG")) u_RegFile (
    .WriteData(RegWD), .ReadAddr1(instr[25:21]), .ReadAddr2(instr[20:16]), .WriteAddr(RegWAddr),
    .RegWrite(RegWrite), .Clock(CLK), .Reset(RST), .ReadData1(RegData1), .ReadData2(MemWD));
  DMem #(.applicationType("IVERILOG")) u_DMem (
    .Address(ALUResult), .WriteData(MemWD), .MemWrite(MemWrite), .MemRead(MemRead), .ReadData(MemData));
  PC #(.applicationType("IVERILOG")) u_PC (.clock(CLK), .nextPC(NextPC), .PC(PC));
  IMem #(.applicationType("IVERILOG")) u_IMem (.address(PC), .i_out({instr, immediate, funct}));
  Multiplexer #(.Selector_Bits(2), .Bits(5)) multiplexer_4 (
    .sel(RegDst), .in_0(instr[20:16]), .in_1(immediate[15:11]), .in_2(5'b00001), .in_3({5{1'b0}}),
    .out(RegWAddr));
  Multiplexer #(.Bits(32)) multiplexer_5 (.sel(Jal), .in_0(ALUMem), .in_1({PCPlus4, PCJump}), .out(RegWD));
  Multiplexer #(.Bits(32)) multiplexer_6 (.sel(UseShamt), .in_0(RegData1), .in_1(sign__shamt), .out(In1));
  Multiplexer #(.Selector_Bits(2), .Bits(32)) multiplexer_7 (
    .sel(ALUSrc), .in_0(MemWD), .in_1(sign__imm), .in_2({{16{1'b0}}, immediate, funct}),
    .in_3({{16{1'b0}}, immediate, funct}), .out(In2));
  Control #(.applicationType("IVERILOG")) u_Control (
    .OPCODE(instr[31:26]), .MemtoReg(MemToReg), .MemRead(MemRead), .RegWrite(RegWrite), .Branch(Branch),
    .Brchne(BranchNe), .MemWrite(MemWrite), .Jump(Jump), .Jal(Jal), .RegDst(RegDst), .ALUSrc(ALUSrc),
    .ALUOp(ALUOp));
  Ula #(.applicationType("IVERILOG")) u_Ula (.In1(In1), .In2(In2), .OP(Op), .result(ALUResult), .Zero_flag(zero));
  UlaCtrl #(.applicationType("IVERILOG")) u_UlaCtrl (
    .ALUOp(ALUOp), .func(funct), .operation(Op), .shamt(UseShamt), .JR(JumpRegister));
  Multiplexer #(.Bits(32)) multiplexer_8 (.sel(MemToReg), .in_0(ALUResult), .in_1(MemData), .out(ALUMem));

  // Other names for the same wires on the sheet: immediate[5:0] = funct; instr[15:0] = {immediate, funct};
  //   j__address[25:0] = {instr[25:16], immediate, funct}; PCJump[25:0] = {instr[25:16], immediate, funct};
  //   s__j__addr[25:0] = {instr[25:16], immediate, funct}; upper__imm[15:0] = {immediate, funct};
  //   zero__imm[15:0] = {immediate, funct}; shamt[4:0] = immediate[10:6]; rd[4:0] = immediate[15:11];
  //   RegAddr2[4:0] = instr[20:16]; rt[4:0] = instr[20:16]; RegAddr1[4:0] = instr[25:21]; rs[4:0] = instr[25:21];
  //   opcode[5:0] = instr[31:26]; ALUOut[31:0] = ALUResult; MemAddr[31:0] = ALUResult; PCPlus4[3:0] = PCJump;
  //   RegData2[31:0] = MemWD

  // Notes on the sheet:
  //   Clock, Reset e Outputs
  //   Cálculo do PCSrc
  //   Cálculo PCBranch
  //   Cálculo PCJump
  //   Parse das Instruções de 32-bits
  //   Atualização do PC
  //   Entradas do regifle
  //   Módulos Verilog
  //   Entradas do ALU
  //   Entradas da d\_mem
  //   ALUMem
endmodule

/* Code of Shift32:
module Shift32(
   input [31:0] a, 
   shamt,
   output [31:0] out);

   assign out = a << shamt;
endmodule
*/

/* Code of Addr32_1:
module Addr32_1(
   input [31:0] a, 
   b,
   output [31:0] out);

   assign out = a + b;
endmodule
*/

/* Code of Addr32_0:
module Addr32_0(
   input [31:0] a, 
   b,
   output [31:0] out);

   assign out = a + b;
endmodule
*/

/* Code of RegFile:
module RegFile (ReadAddr1, ReadAddr2, ReadData1, ReadData2, WriteAddr, WriteData, RegWrite, Clock, Reset);
	
	output  wire [31:0] ReadData1;
	output  wire [31:0] ReadData2;
	input wire [31:0] WriteData;
	input wire [4:0] ReadAddr1;
	input wire [4:0] ReadAddr2;
	input wire [4:0] WriteAddr;
	input wire RegWrite, Clock, Reset;
	
	reg [31:0] regs [31:0];
	
	initial begin
    	regs[0] = 0;
    	regs[1] = 0;
    	regs[2] = 0;
    	regs[3] = 0;
    	regs[4] = 0;
    	regs[5] = 0;
    	regs[6] = 0;
    	regs[7] = 0;
    	regs[8] = 0;
    	regs[9] = 0;
    	regs[10] = 0;
    	regs[11] = 0;
    	regs[12] = 0;
    	regs[13] = 0;
    	regs[14] = 0;
    	regs[15] = 0;
    	regs[16] = 0;
    	regs[17] = 0;
    	regs[18] = 0;
    	regs[19] = 0;
    	regs[20] = 0;
    	regs[21] = 0;
    	regs[22] = 0;
    	regs[23] = 0;
    	regs[24] = 0;
    	regs[25] = 0;
    	regs[26] = 0;
    	regs[27] = 0;
    	regs[28] = 0;
    	regs[29] = 0;
    	regs[30] = 0;
    	regs[31] = 0;
  end
  

	integer i;

	always@ (posedge Clock, posedge Reset) begin
		if (Reset) 
			for (i = 0; i < 32; i = i + 1)
				regs[i] <= 0;
		else if (RegWrite && WriteAddr!= 0)
			regs[WriteAddr] <= WriteData;
	end
	
	assign ReadData1 = (ReadAddr1 == 0) ? 0 : regs[ReadAddr1];
   assign ReadData2 = (ReadAddr2 == 0) ? 0 : regs[ReadAddr2];

endmodule
*/

/* Code of DMem:
module DMem (Address, WriteData, ReadData, MemWrite, MemRead);

	input wire [31:0] Address;
	input wire [31:0] WriteData;
	output wire [31:0] ReadData;
	input wire MemWrite;
	input wire MemRead;
	
	reg [31:0] data [0:127];
	
	integer i;
    

    initial begin
      for (i = 0; i < 128; i = i + 1) begin
        data[i] <= 0;
      end
    end	
	
	always @ (*) begin
		if (MemWrite == 1)
			data[Address] <= WriteData;			
	end

	assign ReadData = (MemRead == 0) ? 0 : data[Address];


endmodule
*/

/* Code of PC:
module PC(clock, nextPC, PC);

	input clock;
	input [31:0] nextPC;
	
	output reg [31:0] PC;
	
	always @(posedge clock) begin
			PC <= nextPC; 
	end
endmodule
*/

/* Code of IMem:
module IMem (address, i_out);

	input wire [31:0] address;
	output wire [31:0] i_out;
	
	reg [31:0] instructions[0:127];
	
	initial begin
		$readmemb("instruction.list", instructions);
	end
	
	assign i_out = instructions[address];


endmodule
*/

/* Code of Control:
module Control (OPCODE, MemRead, RegWrite, RegDst, ALUSrc, Branch, Brchne, MemWrite, MemtoReg, Jump, Jal, ALUOp);

	input wire [5:0] OPCODE;
	output reg MemtoReg, MemRead, RegWrite, Branch, Brchne, MemWrite, Jump, Jal;
	output reg [1:0] RegDst, ALUSrc;
	output reg [2:0] ALUOp;
	
	always @(*) begin
		case(OPCODE)
			0: begin
                RegWrite <= 1'b1;
                RegDst <= 2'b01;
                ALUSrc <= 2'b00;
                Branch <= 1'b0;
                Brchne <= 1'b0;
                MemWrite <= 1'b0;
                MemtoReg <= 2'b00;
                Jump <= 1'b0;
                Jal <= 1'b0;
                ALUOp <= 3'b110;
                MemRead <= 1'b0;
			end
			35: begin
                RegWrite <= 1'b1;
                RegDst <= 2'b00;
                ALUSrc <= 2'b01;
                Branch <= 1'b0;
                Brchne <= 1'b0;
                MemWrite <= 1'b0;
                MemtoReg <= 2'b01;
                Jump <= 1'b0;
                Jal <= 1'b0;
                ALUOp <= 3'b000;
                MemRead <= 1'b1;
			end
			43: begin
                RegWrite <= 1'b0;
                RegDst <= 2'bxx;
                ALUSrc <= 2'b01;
                Branch <= 1'b0;
                Brchne <= 1'b0;
                MemWrite <= 1'b1;
                MemtoReg <= 2'bxx;
                Jump <= 1'b0;
                Jal <= 1'b0;
                ALUOp <= 3'b000;
                MemRead <= 1'b0;
			end
			4: begin
                RegWrite <= 1'b0;
                RegDst <= 2'bxx;
                ALUSrc <= 2'b00;
                Branch <= 1'b1;
                Brchne <= 1'b0;
                MemWrite <= 1'b0;
                MemtoReg <= 2'bxx;
                Jump <= 1'b0;
                Jal <= 1'b0;
                ALUOp <= 3'b001;
                MemRead <= 1'b0;
			end
            5: begin
                RegWrite <= 1'b0;
                RegDst <= 2'bxx;
                ALUSrc <= 2'b00;
                Branch <= 1'b0;
                Brchne <= 1'b1;
                MemWrite <= 1'b0;
                MemtoReg <= 2'bxx;
                Jump <= 1'b0;
                Jal <= 1'b0;
                ALUOp <= 3'b001;
                MemRead <= 1'b0;
			end
            8: begin
                RegWrite <= 1'b1;
                RegDst <= 2'b00;
                ALUSrc <= 2'b01;
                Branch <= 1'b0;
                Brchne <= 1'b0;
                MemWrite <= 1'b0;
                MemtoReg <= 2'b00;
                Jump <= 1'b0;
                Jal <= 1'b0;
                ALUOp <= 3'b000;
                MemRead <= 1'b0;
			end
            2: begin
                RegWrite <= 1'b0;;
                RegDst <= 2'bxx;
                ALUSrc <= 2'bxx;
                Branch <= 1'bx;
                Brchne <= 1'bx;
                MemWrite <= 1'b0;
                MemtoReg <= 2'bxx;
                Jump <= 1'b1;
                Jal <= 1'b0;
                ALUOp <= 3'bxxx;
                MemRead <= 1'b0;
			end
            3: begin
                RegWrite <= 1'b1;
                RegDst <= 2'b10;
                ALUSrc <= 2'bxx;
                Branch <= 1'bx;
                Brchne <= 1'bx;
                MemWrite <= 1'b0;
                MemtoReg <= 2'bxx;
                Jump <= 1'b1;
                Jal <= 1'b1;
                ALUOp <= 3'bxxx;
                MemRead <= 1'b0;
			end
            12: begin
                RegWrite <= 1'b1;
                RegDst <= 2'b00;
                ALUSrc <= 2'b10;
                Branch <= 1'b0;
                Brchne <= 1'b0;
                MemWrite <= 1'b0;
                MemtoReg <= 2'b00;
                Jump <= 1'b0;
                Jal <= 1'b0;
                ALUOp <= 3'b010;
                MemRead <= 1'b0;
			end
            13: begin
                RegWrite <= 1'b1;
                RegDst <= 2'b00;
                ALUSrc <= 2'b10;
                Branch <= 1'b0;
                Brchne <= 1'b0;
                MemWrite <= 1'b0;
                MemtoReg <= 2'b00;
                Jump <= 1'b0;
                Jal <= 1'b0;
                ALUOp <= 3'b011;
                MemRead <= 1'b0;
			end
            14: begin
                RegWrite <= 1'b1;
                RegDst <= 2'b00;
                ALUSrc <= 2'b10;
                Branch <= 1'b0;
                Brchne <= 1'b0;
                MemWrite <= 1'b0;
                MemtoReg <= 2'b00;
                Jump <= 1'b0;
                Jal <= 1'b0;
                ALUOp <= 3'b100;
                MemRead <= 1'b0;
			end
            10: begin
                RegWrite <= 1'b1;
                RegDst <= 2'b00;
                ALUSrc <= 2'b01;
                Branch <= 1'b0;
                Brchne <= 1'b0;
                MemWrite <= 1'b0;
                MemtoReg <= 2'b00;
                Jump <= 1'b0;
                Jal <= 1'b0;
                ALUOp <= 3'b101;
                MemRead <= 1'b0;
			end
            11: begin
                RegWrite <= 1'b1;
                RegDst <= 2'b00;
                ALUSrc <= 2'b01;
                Branch <= 1'b0;
                Brchne <= 1'b0;
                MemWrite <= 1'b0;
                MemtoReg <= 2'b00;
                Jump <= 1'b0;
                Jal <= 1'b0;
                ALUOp <= 3'b101;
                MemRead <= 1'b0;
			end
            15: begin
                RegWrite <= 1'b1;
                RegDst <= 2'b00;
                ALUSrc <= 2'b11;
                Branch <= 1'b0;
                Brchne <= 1'b0;
                MemWrite <= 1'b0;
                MemtoReg <= 2'b00;
                Jump <= 1'b0;
                Jal <= 1'b0;
                ALUOp <= 3'b000;
                MemRead <= 1'b0;
			end
		endcase
	end

endmodule
*/

/* Code of Ula:
module Ula (In1, In2, OP, result, Zero_flag);
	
	input wire [31:0] In1;
	input wire [31:0] In2;
	input wire [3:0] OP;
	output reg [31:0] result;
	output wire Zero_flag;
	
	assign Zero_flag = (result == 0);

	always@ (*) begin
			
		case (OP)
			 0: result <= In1 + In2; 
          1: result <= In1 - In2;
          3: result <= In1 & In2; 
          4: result <= ~(In1 | In2); 
          5: result <= In1 | In2;
          6: result <= In1 ^ In2; 
          7: result <= In2 << (In1); 
          8: result <= In1 << (In2); 
          9: result <= In2 >> (In1); 
          10: result <= In1 >> (In2); 
          12: result <= In2 >>> (In1); 
          13: result <= In1 >>> (In2); 
          14: result <=  ($signed(In1) < $signed(In2)) ? 1 : 0; 
          15: result <= (In1 < In2) ? 1 : 0 ;
        default: result <= 0;
		endcase
	end

endmodule
*/

/* Code of UlaCtrl:
module UlaCtrl (ALUOp, func, operation, shamt, JR);

	input wire [2:0] ALUOp;
	input wire [5:0] func;
	output reg [3:0] operation;
	output wire shamt, JR;
	
	reg [3:0] OpCheck;

	always @(*) begin
        case(ALUOp)
            0: operation = 0; 
            1: operation = 1; 
            2: operation = 3; 
            3: operation = 5; 
            4: operation = 6; 
            5: operation = 14; 
            6: operation = OpCheck; 
            7: operation = 15; 
            default: operation = 0; 
        endcase
    end

    always @(*) begin
        case(func)
            0: OpCheck <= 7; 
            2:  OpCheck <= 9; 
            3: OpCheck <= 12; 
            4: OpCheck <= 8;
            6: OpCheck <= 10; 
            7: OpCheck <= 13;
            32: OpCheck <= 0; 
            34: OpCheck <= 1;
            36: OpCheck <= 3;
            37: OpCheck <= 5;  
            38: OpCheck <= 6; 
            39: OpCheck <= 4; 
            42: OpCheck <= 14; 
            43: OpCheck <= 15; 
            default: OpCheck <= 0;
        endcase
    end

    assign JR = (ALUOp == 6) ? ((func == 8) ? 1 : 0) : 0;
    assign shamt = (ALUOp == 6) ? ((func == 0 || func == 2 || func == 3) ? 1 : 0) : 0;

endmodule
*/
